# Fritzing sketch ELED (saved by Fritzing 0.9.3b)
circuit board: 9.43837cm x 6.82885cm
breadboards: 1

parts:
  Componente1 = Arduino Uno (Rev3)
  R1 = PHOTOCELL [package=photocell-kit]
  R2 = PHOTOCELL [package=photocell-kit]
  R3 = PHOTOCELL [package=photocell-kit]
  R4 = PHOTOCELL [package=photocell-kit]
  R5 = Resistor [tolerance=±5% resistance=220 package="2010 [SMD]"]
  R6 = Resistor [tolerance=±5% resistance=220 package="2010 [SMD]"]
  R7 = Resistor [tolerance=±5% resistance=220 package="2010 [SMD]"]
  R8 = Resistor [tolerance=±5% resistance=220 package="2010 [SMD]"]
  J1 = Basic Servo
  J2 = Basic Servo

nets:
  N1: Componente1.A0, R1.P$2, R5.Pin_0
  N2: Componente1.A1, R2.P$2, R6.Pin_0
  N3: Componente1.A2, R3.P$2, R7.Pin_0
  N4: Componente1.A3, R4.P$2, R8.Pin_0
  GND: Componente1.GND, R5.Pin_1, R6.Pin_1, R7.Pin_1, R8.Pin_1, J1.gnd, J2.gnd
  N5: Componente1.D6_PWM, J2.pulse
  N6: Componente1.D7, J1.pulse
  VCC: Componente1.5V, R1.P$1, R2.P$1, R3.P$1, R4.P$1, J1.vcc, J2.vcc
